// Logisim project logism ic circuit.circ as structural Verilog: 1 circuit, main circuit main
module main (
);

  wire button_1_out, n7402_1_pin7, n7402_1_pin8, n7402_1_pin9, n7402_1_pin10, n7402_1_pin11, n7402_1_pin12,
       n7402_1_pin13, n7402_1_pin14, n7404_1_pin1, n7404_1_pin2, n7404_1_pin6, n7404_1_pin7, n7404_1_pin14,
       n7408_1_pin2, n7408_1_pin7, n7408_1_pin8, n7408_1_pin14, n7432_1_pin3, n7432_1_pin4, n7432_1_pin6,
       n7432_1_pin7, n7432_1_pin14, n7447_1_pin8, n7447_1_pin9, n7447_1_pin10, n7447_1_pin11, n7447_1_pin12,
       n7447_1_pin13, n7447_1_pin14, n7447_1_pin15, n7447_1_pin16, n74193_1_pin1, n74193_1_pin4,
       n74193_1_pin5, n74193_1_pin9, n74193_1_pin10, n74193_1_pin11, n74193_1_pin14, n74193_1_pin15,
       nor_1_out;

  _7402 #(.VccGndPorts("true")) u_7402_1 (
    .pin7(n7402_1_pin7), .pin14(n7402_1_pin14), .pin13(n7402_1_pin13), .pin12(n7402_1_pin12),
    .pin11(n7402_1_pin11), .pin10(n7402_1_pin10), .pin9(n7402_1_pin9), .pin8(n7402_1_pin8));  // open: pin1, pin2, pin3, pin4, pin5, pin6
  Button button_1 (.out(button_1_out));
  _74193 u_74193_1 (
    .pin1(n74193_1_pin1), .pin2(n7402_1_pin9), .pin3(n7402_1_pin8), .pin4(n74193_1_pin4),
    .pin5(n74193_1_pin5), .pin6(n7402_1_pin12), .pin7(n7402_1_pin11), .pin15(n74193_1_pin15),
    .pin14(n74193_1_pin14), .pin11(n74193_1_pin11), .pin10(n74193_1_pin10), .pin9(n74193_1_pin9));  // open: pin13, pin12
  _7447 #(.VccGndPorts("true")) u_7447_1 (
    .pin1(n7402_1_pin9), .pin2(n7402_1_pin12), .pin6(n7402_1_pin11), .pin7(n7402_1_pin8),
    .pin8(n7447_1_pin8), .pin16(n7447_1_pin16), .pin15(n7447_1_pin15), .pin14(n7447_1_pin14),
    .pin13(n7447_1_pin13), .pin12(n7447_1_pin12), .pin11(n7447_1_pin11), .pin10(n7447_1_pin10),
    .pin9(n7447_1_pin9));  // open: pin3, pin4, pin5
  _7404 #(.VccGndPorts("true")) u_7404_1 (
    .pin1(n7404_1_pin1), .pin2(n7404_1_pin2), .pin3(button_1_out), .pin4(n74193_1_pin11),
    .pin5(n7402_1_pin11), .pin6(n7404_1_pin6), .pin7(n7404_1_pin7), .pin14(n7404_1_pin14));  // open: pin13, pin12, pin11, pin10, pin9, pin8
  _7_Segment_Display #(.active("false")) u_7_segment_display_1 (
    .g(n7447_1_pin14), .f(n7447_1_pin15), .a(n7447_1_pin13), .b(n7447_1_pin12), .e(n7447_1_pin9),
    .d(n7447_1_pin10), .c(n7447_1_pin11));  // open: dp
  _7432 #(.VccGndPorts("true")) u_7432_1 (
    .pin1(n7404_1_pin2), .pin2(button_1_out), .pin3(n7432_1_pin3), .pin4(n7432_1_pin4), .pin5(n7402_1_pin12),
    .pin6(n7432_1_pin6), .pin7(n7432_1_pin7), .pin14(n7432_1_pin14));  // open: pin13, pin12, pin11, pin10, pin9, pin8
  nor nor_1 (nor_1_out, n7408_1_pin8, n7404_1_pin1);
  _7408 #(.VccGndPorts("true")) u_7408_1 (
    .pin1(n7432_1_pin3), .pin2(n7408_1_pin2), .pin3(n74193_1_pin4), .pin4(n7402_1_pin8), .pin5(n7402_1_pin9),
    .pin6(n7432_1_pin4), .pin7(n7408_1_pin7), .pin14(n7408_1_pin14), .pin13(n7402_1_pin10),
    .pin12(n7402_1_pin13), .pin11(n7404_1_pin1), .pin10(n7404_1_pin6), .pin9(n7432_1_pin6),
    .pin8(n7408_1_pin8));
  Clock clock_1 (.out(n7408_1_pin2));
  LED led_1 (.in(n7408_1_pin8));
  LED led_2 (.in(nor_1_out));
  LED led_3 (.in(n7404_1_pin1));
  // also tied to GND on the sheet: {n74193_1_pin1, n74193_1_pin14, n7402_1_pin7, n74193_1_pin10, n7447_1_pin8, n7404_1_pin7, n7432_1_pin7, n7408_1_pin7}
  // also tied to VCC on the sheet: {n7402_1_pin14, n74193_1_pin15, n74193_1_pin5, n74193_1_pin9, n7447_1_pin16, n7404_1_pin14, n7432_1_pin14, n7408_1_pin14}
endmodule
